// Digital circuit register-file.dig as structural Verilog
module register_file (
  input  [4:0] ReadReg1,
  input  [4:0] ReadReg2,
  input  [4:0] WriteReg,
  input  [31:0] WriteData,
  input  RegWrite,
  input  Clock,
  output [31:0] ReadData1,
  output [31:0] ReadData2
);

  wire D1, D2, D3, D4, D5, D6, D7, D8, D9, D10, D11, D12, D13, D14, D15, D16, D17, D18, D19, D20, D21, D22,
       D23, D24, D25, D26, D27, D28, D29, D30, D31;
  wire [31:0] Q1, Q2, Q3, Q4, Q5, Q6, Q7, Q8, Q9, Q10, Q11, Q12, Q13, Q14, Q15, Q16, Q17, Q18, Q19, Q20, Q21,
       Q22, Q23, Q24, Q25, Q26, Q27, Q28, Q29, Q30, Q31;

  Decoder #(.Selector_Bits(5)) WriteDecoder (
    .out_1(D1), .out_2(D2), .out_3(D3), .out_4(D4), .out_5(D5), .out_6(D6), .out_7(D7), .out_8(D8),
    .out_9(D9), .out_10(D10), .out_11(D11), .out_12(D12), .out_13(D13), .out_14(D14), .out_15(D15),
    .out_16(D16), .out_17(D17), .out_18(D18), .out_19(D19), .out_20(D20), .out_21(D21), .out_22(D22),
    .out_23(D23), .out_24(D24), .out_25(D25), .out_26(D26), .out_27(D27), .out_28(D28), .out_29(D29),
    .out_30(D30), .out_31(D31));  // open: sel, out_0
  and and_1 (Clock, RegWrite, D1);
  and and_2 (Clock, RegWrite, D2);
  and and_3 (Clock, RegWrite, D3);
  and and_4 (Clock, RegWrite, D4);
  and and_5 (Clock, RegWrite, D5);
  and and_6 (Clock, RegWrite, D6);
  and and_7 (Clock, RegWrite, D7);
  and and_8 (Clock, RegWrite, D8);
  and and_9 (Clock, RegWrite, D9);
  and and_10 (Clock, RegWrite, D10);
  and and_11 (Clock, RegWrite, D11);
  and and_12 (Clock, RegWrite, D12);
  and and_13 (Clock, RegWrite, D13);
  and and_14 (Clock, RegWrite, D14);
  and and_15 (Clock, RegWrite, D15);
  and and_16 (Clock, RegWrite, D16);
  and and_17 (Clock, RegWrite, D17);
  and and_18 (Clock, RegWrite, D18);
  and and_19 (Clock, RegWrite, D19);
  and and_20 (Clock, RegWrite, D20);
  and and_21 (Clock, RegWrite, D21);
  and and_22 (Clock, RegWrite, D22);
  and and_23 (Clock, RegWrite, D23);
  and and_24 (Clock, RegWrite, D24);
  and and_25 (Clock, RegWrite, D25);
  and and_26 (Clock, RegWrite, D26);
  and and_27 (Clock, RegWrite, D27);
  and and_28 (Clock, RegWrite, D28);
  and and_29 (Clock, RegWrite, D29);
  and and_30 (Clock, RegWrite, D30);
  and and_31 (Clock, RegWrite, D31);
  Register #(.Bits(32)) R0 (.D(WriteData), .C(Clock));  // open: en, Q
  Register #(.Bits(32)) R1 (.D(WriteData), .C(Clock));  // open: en, Q
  Register #(.Bits(32)) R2 (.D(WriteData), .C(Clock));  // open: en, Q
  Register #(.Bits(32)) R3 (.D(WriteData), .C(Clock));  // open: en, Q
  Register #(.Bits(32)) R4 (.D(WriteData), .C(Clock));  // open: en, Q
  Register #(.Bits(32)) R5 (.D(WriteData), .C(Clock));  // open: en, Q
  Register #(.Bits(32)) R6 (.D(WriteData), .C(Clock));  // open: en, Q
  Register #(.Bits(32)) R7 (.D(WriteData), .C(Clock));  // open: en, Q
  Register #(.Bits(32)) R8 (.D(WriteData), .C(Clock));  // open: en, Q
  Register #(.Bits(32)) R9 (.D(WriteData), .C(Clock));  // open: en, Q
  Register #(.Bits(32)) R10 (.D(WriteData), .C(Clock));  // open: en, Q
  Register #(.Bits(32)) R11 (.D(WriteData), .C(Clock));  // open: en, Q
  Register #(.Bits(32)) R12 (.D(WriteData), .C(Clock));  // open: en, Q
  Register #(.Bits(32)) R13 (.D(WriteData), .C(Clock));  // open: en, Q
  Register #(.Bits(32)) R14 (.D(WriteData), .C(Clock));  // open: en, Q
  Register #(.Bits(32)) R15 (.D(WriteData), .C(Clock));  // open: en, Q
  Register #(.Bits(32)) R16 (.D(WriteData), .C(Clock));  // open: en, Q
  Register #(.Bits(32)) R17 (.D(WriteData), .C(Clock));  // open: en, Q
  Register #(.Bits(32)) R18 (.D(WriteData), .C(Clock));  // open: en, Q
  Register #(.Bits(32)) R19 (.D(WriteData), .C(Clock));  // open: en, Q
  Register #(.Bits(32)) R20 (.D(WriteData), .C(Clock));  // open: en, Q
  Register #(.Bits(32)) R21 (.D(WriteData), .C(Clock));  // open: en, Q
  Register #(.Bits(32)) R22 (.D(WriteData), .C(Clock));  // open: en, Q
  Register #(.Bits(32)) R23 (.D(WriteData), .C(Clock));  // open: en, Q
  Register #(.Bits(32)) R24 (.D(WriteData), .C(Clock));  // open: en, Q
  Register #(.Bits(32)) R25 (.D(WriteData), .C(Clock));  // open: en, Q
  Register #(.Bits(32)) R26 (.D(WriteData), .C(Clock));  // open: en, Q
  Register #(.Bits(32)) R27 (.D(WriteData), .C(Clock));  // open: en, Q
  Register #(.Bits(32)) R28 (.D(WriteData), .C(Clock));  // open: en, Q
  Register #(.Bits(32)) R29 (.D(WriteData), .C(Clock));  // open: en, Q
  Register #(.Bits(32)) R30 (.D(WriteData), .C(Clock));  // open: en, Q
  Register #(.Bits(32)) R31 (.D(WriteData), .C(Clock));  // open: en, Q
  Multiplexer #(.Selector_Bits(5), .Bits(32)) ReadMux1 (
    .sel(ReadReg1), .in_0({32{1'b0}}), .in_1(Q1), .in_2(Q2), .in_3(Q3), .in_4(Q4), .in_5(Q5), .in_6(Q6),
    .in_7(Q7), .in_8(Q8), .in_9(Q9), .in_10(Q10), .in_11(Q11), .in_12(Q12), .in_13(Q13), .in_14(Q14),
    .in_15(Q15), .in_16(Q16), .in_17(Q17), .in_18(Q18), .in_19(Q19), .in_20(Q20), .in_21(Q21), .in_22(Q22),
    .in_23(Q23), .in_24(Q24), .in_25(Q25), .in_26(Q26), .in_27(Q27), .in_28(Q28), .in_29(Q29), .in_30(Q30),
    .in_31(Q31), .out(ReadData1));
  Multiplexer #(.Selector_Bits(5), .Bits(32)) ReadMux2 (
    .sel(ReadReg2), .in_0({32{1'b0}}), .in_1(Q1), .in_2(Q2), .in_3(Q3), .in_4(Q4), .in_5(Q5), .in_6(Q6),
    .in_7(Q7), .in_8(Q8), .in_9(Q9), .in_10(Q10), .in_11(Q11), .in_12(Q12), .in_13(Q13), .in_14(Q14),
    .in_15(Q15), .in_16(Q16), .in_17(Q17), .in_18(Q18), .in_19(Q19), .in_20(Q20), .in_21(Q21), .in_22(Q22),
    .in_23(Q23), .in_24(Q24), .in_25(Q25), .in_26(Q26), .in_27(Q27), .in_28(Q28), .in_29(Q29), .in_30(Q30),
    .in_31(Q31), .out(ReadData2));

  // Other names for the same wires on the sheet: CLK = Clock; RD1[31:0] = ReadData1; RD2[31:0] = ReadData2;
  //   RR1[4:0] = ReadReg1; RR2[4:0] = ReadReg2; RW = RegWrite; WD[31:0] = WriteData; WR[4:0] = WriteReg
endmodule

/* Test case Register File Test:
WriteReg WriteData RegWrite Clock ReadReg1 ReadReg2 ReadData1 ReadData2

# $1 = 25
1 25 1 C 1 0 25 0

# $2 = 30
2 30 1 C 0 2 0 30

# $(N+1) = (N+1)
loop(N, 30)
	(N+1) (N+1) 1 C (N+1) (N) (N+1) (N)
end loop

# $(N+1) = N-60
loop(N, 30)
	(N+1) (N-60) 1 C (N+1) (N+1) (N-60) (N-60)
end loop

# Try writing to $0. This should not write anything
0 25 1 C 0 0 0 0

# try writing when RegWrite = 0
# (the registers should still have their old values)
loop(N, 30)
	(N+1) (N+80) 0 C (N+1) (N+1) (N-60) (N-60)
end loop
*/
